# Fritzing sketch Lightsaber (saved by Fritzing 0.9.2b)
breadboards: 1

parts:
  SP1 = SPEAKER [package=pcb_mount_speaker]
  Q1 = NPN-Transistor [part_number=2N3904 package="TO92 [THT]"]
  Arduino_Pro_Mini_3_3_V = Arduino Pro Mini v13
  S1 = Pushbutton [package=THT]
  BAT1 = Battery Holders [package=battery-aa-panel]
  LED1 = LEDs [package=led10mm]
  PIEZO_SENSOR = Piezo Sensor
  BUCK_PUCK = mystery part, 4 pins [chip_label=?]
  RECHARGE_PORT = mystery part, 3 pins [chip_label=?]
  R4 = Resistor [tolerance=±5% resistance=1M package=THT]
  R1 = Resistor [tolerance=±5% resistance=10 package=THT]
  R3 = Resistor [tolerance=±5% resistance=1M package=THT]
  Q2 = Basic FET N-Channel [part_number=FQP30N06L package="TO220 [THT]"]
  C1 = Electrolytic Capacitor [capacitance=100μF package="0807 [SMD, electrolytic]"]
  R2 = Resistor [tolerance=±5% resistance=10 package=THT]

nets:
  N1: SP1.+, C1.-
  N2: SP1.-, Arduino_Pro_Mini_3_3_V.GND, S1.leg0, PIEZO_SENSOR.pin2, RECHARGE_PORT.pin1, R4.Pin_1, R3.Pin_1, Q2.source, R2.Pin_0
  N3: Q1.E, R1.Pin_0
  N4: Q1.B, Arduino_Pro_Mini_3_3_V.D11_PWM/MOSI
  N5: Q1.C, Arduino_Pro_Mini_3_3_V.VCC, BAT1.+, BUCK_PUCK.pin1, RECHARGE_PORT.pin3, C1.+
  N6: Arduino_Pro_Mini_3_3_V.A0, PIEZO_SENSOR.pin1, R4.Pin_0
  N7: Arduino_Pro_Mini_3_3_V.D10_PWM/SS, R3.Pin_0, Q2.gate
  N8: Arduino_Pro_Mini_3_3_V.D2, S1.leg1
  N9: BAT1.-, RECHARGE_PORT.pin2
  N10: LED1.A, BUCK_PUCK.pin3
  N11: LED1.C, BUCK_PUCK.pin4
  N12: BUCK_PUCK.pin2, Q2.drain
  N13: R1.Pin_1, R2.Pin_1

custom parts:
  Piezo Sensor: Piezo
