# Fritzing sketch LightsaberBreakout v1 (saved by Fritzing 0.9.2b)
circuit board: 6.83333cm x 2.44338cm
breadboards: 1

parts:
  SP1 = SPEAKER [package=pcb_mount_speaker]
  Q1 = NPN-Transistor [part_number=2N3904 package="TO92 [THT]"]
  R1 = Resistor [tolerance=±5% resistance=220 package=THT]
  Q2 = Basic FET N-Channel [part_number=FQP30N06L package="TO220 [THT]"]
  PIEZO = Piezo Sensor
  R3 = Resistor [tolerance=±5% resistance=10k package=THT]
  R4 = Resistor [tolerance=±5% resistance=1M package=THT]
  R2 = Resistor [tolerance=±5% resistance=37 package=THT]
  JP2 = Header 4 [package=1x04-smd]
  JP1 = Header 6 [package=1x06-smd]

nets:
  N1: SP1.+, JP2.1, JP1.VCC
  N2: SP1.-, R2.Pin_0
  N3: Q1.E, Q2.source, PIEZO.pin2, R3.Pin_1, R4.Pin_0, JP2.3, JP1.GND
  N4: Q1.B, R1.Pin_1
  N5: Q1.C, R2.Pin_1
  N6: R1.Pin_0, JP1.SPEAKER
  N7: Q2.gate, R3.Pin_0, JP1.LED
  N8: Q2.drain, JP2.2
  N9: PIEZO.pin1, R4.Pin_1, JP1.PIEZO
  N10: JP2.4, JP1.SWITCH

custom parts:
  Piezo Sensor: Piezo
  Header 6: Header 6 Standard 6-pin 0.1 header. Use with straight break away headers (SKU : PRT-00116), right angle break away headers (PRT-00553), swiss pins (PRT-00743), machine pins (PRT-00117), and female headers (PRT-00115). Molex polarized connector foot print use with SKU : PRT-08094 with associated crimp pins and housings. NOTES ON THE VARIANTS LOCK and LOCK_LONGPADS... This footprint was designed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
