# Fritzing sketch LightsaberBreakout v2 (saved by Fritzing 0.9.2b)
breadboards: 1

parts:
  Q1_TRANSISTOR = NPN-Transistor [part_number=2N3904 package="TO92 [THT]"]
  Arduino_Pro_Mini_3_3_V = Arduino Pro Mini v13
  R1 = Resistor [tolerance=±5% resistance=1k package=THT]
  BAT1 = Battery Holders [package=battery-aa-panel]
  Q2_MOSFET = Basic FET N-Channel [part_number=FQP30N06L package="TO220 [THT]"]
  PIEZO_SENSOR = Piezo Sensor
  R3 = Resistor [tolerance=±5% resistance=10k package=THT]
  RECHARGE_PORT = mystery part, 3 pins [chip_label=?]
  R4 = Resistor [tolerance=±5% resistance=1M package=THT]
  R2 = Resistor [tolerance=±5% resistance=37 package=THT]
  JP1 = Header 4 [package=1x04-smd]
  SP1 = SPEAKER [package=pcb_mount_speaker]

nets:
  N1: Q1_TRANSISTOR.E, Arduino_Pro_Mini_3_3_V.GND, Q2_MOSFET.source, PIEZO_SENSOR.pin2, R3.Pin_1, RECHARGE_PORT.pin1, R4.Pin_1, JP1.SW_(-)
  N2: Q1_TRANSISTOR.B, R1.Pin_1
  N3: Q1_TRANSISTOR.C, R2.Pin_1
  N4: Arduino_Pro_Mini_3_3_V.VCC, BAT1.+, RECHARGE_PORT.pin3, JP1.LED_(+), SP1.+
  N5: Arduino_Pro_Mini_3_3_V.A0, PIEZO_SENSOR.pin1, R4.Pin_0
  N6: Arduino_Pro_Mini_3_3_V.D11_PWM/MOSI, R1.Pin_0
  N7: Arduino_Pro_Mini_3_3_V.D10_PWM/SS, Q2_MOSFET.gate, R3.Pin_0
  N8: Arduino_Pro_Mini_3_3_V.D2, JP1.SW_(+)
  N9: BAT1.-, RECHARGE_PORT.pin2
  N10: Q2_MOSFET.drain, JP1.LED_(-)
  N11: R2.Pin_0, SP1.-

custom parts:
  Piezo Sensor: Piezo
  Header 4: Header 4 Standard 4-pin 0.1 header. Use with straight break away headers (SKU : PRT-00116), right angle break away headers (PRT-00553), swiss pins (PRT-00743), machine pins (PRT-00117), and female headers (PRT-00115). Molex polarized connector foot print use with SKU : PRT-08231 with associated crimp pins and housings. 1MM SMD Version SKU: PRT-10208
